# Fritzing sketch mega_l298n_nrf (saved by Fritzing 0.9.3b)

parts:
  Part1 = Arduino Mega 2560 (Rev3)
  S2 = H-Bridge with L298N
  Part2 = NRF24L01+ Breakout Board
  M1 = DC Motor
  M2 = DC Motor
  VCC1 = Battery
  BB1 = 4-Line Bi-Directional Level Shifter  # not connected
  Part3 = 9-DOF IMU L3GD20H + LSM303 [part_number=1714]

nets:
  N1: Part1.D21/SCL, Part3.SCL
  N2: Part1.D20/SDA, Part3.SDA
  N3: Part1.D10_PWM, Part2.CE
  N4: Part1.D9_PWM, Part2.CS
  N5: Part1.D8_PWM, S2.ENA
  3V3: Part1.3V3, Part2.VCC
  GND: Part1.GND, Part2.GND, Part3.GND
  N6: Part1.D3_PWM, S2.IN4
  N7: Part1.D4_PWM, S2.IN3
  N8: Part1.D5_PWM, S2.IN2
  N9: Part1.D6_PWM, S2.IN1
  N10: Part1.D7_PWM, S2.ENB
  5V: Part1.5V, Part3.VIN
  N11: Part1.D50, Part2.MISO
  N12: Part1.D51, Part2.MOSI
  N13: Part1.D52, Part2.SCK
  N14: S2.12V, VCC1.+
  N15: S2.GND, VCC1.-
  N16: S2.M1-01, M2.pin_2
  N17: S2.M1-02, M2.pin_1
  N18: S2.M2-01, M1.pin_2
  N19: S2.M2-02, M1.pin_1

custom parts:
  H-Bridge with L298N: h-bridge
  4-Line Bi-Directional Level Shifter: 4-Channel Bi-Directional Level Shifter
  9-DOF IMU L3GD20H + LSM303: This inertial-measurement-unit combines 2 of the best quality sensors available on the market to give you 9 axes of data: 3 axes of accelerometer data, 3 axes gyroscopic, and 3 axes magnetic (compass). We tested many different 'combination' sensors and found these were the best value, with stable and reliable readings.
